# Fritzing sketch telo_hw_schematic (saved by Fritzing 0.9.3b)
breadboards: 1

parts:
  VibMot = Vibration Motor- ROB-08449 [part_number=3V package=vibe-motor-10mm]
  Feather_M0 = Arduino BT [part_number=Bluefruit]
  LiPo = LIPO-1000mAh [part_number=1.2Ah package=lipo-1000]
  TIP31C = npn-Powertransistor [package="TO220 [THT]"]

nets:
  N1: VibMot.+, TIP31C.emitter
  N2: VibMot.-, Feather_M0.GND, LiPo.-
  N3: Feather_M0.PWM_D5, TIP31C.base
  N4: LiPo.+, TIP31C.collector
